# Fritzing sketch Diagrama (saved by Fritzing 0.9.3b)
breadboards: 1

parts:
  Componente1 = Arduino Uno (Rev3)
  PIR1 = PIR sensor
  LED1 = LED - 5mm [color="Red (633nm)" package="5 mm [THT]"]  # not connected
  R1 = Resistor [tolerance=±5% resistance=220 package=THT]

nets:
  N1: Componente1.D12/MISO, PIR1.SIG
  5V: Componente1.5V, PIR1.VDD
  GND: Componente1.GND, PIR1.GND, R1.Pin_1
